// Logisim project aula_13062022.circ as structural Verilog: 2 circuits, main circuit exerc_1
module exerc_1 (
  input  D,
  input  V,
  input  S,
  input  T,
  output La
);

  wire and_1_out, and_2_out, and_3_out, and_4_out, and_5_out, and_6_out, and_7_out, and_8_out, not_1_out,
       not_2_out, not_3_out, not_4_out, not_5_out, not_6_out, not_7_out, not_8_out, not_9_out, not_10_out;

  not not_1 (not_1_out, D);
  not not_2 (not_2_out, V);
  not not_3 (not_3_out, S);
  not not_4 (not_4_out, V);
  not not_5 (not_5_out, T);
  not not_6 (not_6_out, V);
  not not_7 (not_7_out, S);
  not not_8 (not_8_out, T);
  not not_9 (not_9_out, S);
  not not_10 (not_10_out, T);
  and and_1 (and_1_out, not_1_out, V, S, T);
  and and_2 (and_2_out, D, not_2_out, not_3_out, T);
  and and_3 (and_3_out, D, not_4_out, S, not_5_out);
  and and_4 (and_4_out, D, not_6_out, S, T);
  and and_5 (and_5_out, D, V, not_7_out, not_8_out);
  and and_6 (and_6_out, D, V, not_9_out, T);
  and and_7 (and_7_out, D, V, S, not_10_out);
  and and_8 (and_8_out, D, V, S, T);
  or or_1 (La, and_1_out, and_2_out, and_3_out, and_4_out, and_5_out, and_6_out, and_7_out, and_8_out);
endmodule

module exerc_2 (
  input  A,
  input  B,
  input  C,
  input  D,
  output Ab
);

  wire and_1_out, and_2_out, and_3_out, not_1_out, not_2_out, not_3_out, not_4_out, not_5_out, not_6_out,
       not_7_out, not_8_out, not_9_out;

  not not_1 (not_1_out, A);
  not not_2 (not_2_out, B);
  not not_3 (not_3_out, C);
  not not_4 (not_4_out, A);
  not not_5 (not_5_out, B);
  not not_6 (not_6_out, D);
  not not_7 (not_7_out, A);
  not not_8 (not_8_out, C);
  not not_9 (not_9_out, D);
  and and_1 (and_1_out, not_1_out, not_2_out, not_3_out, D);
  and and_2 (and_2_out, not_4_out, not_5_out, C, not_6_out);
  or or_1 (Ab, and_1_out, and_2_out, and_3_out);
  and and_3 (and_3_out, not_7_out, B, not_8_out, not_9_out);
endmodule
